# Fritzing sketch Circuit_Fritzing (saved by Fritzing 0.9.3b)

parts:
  WeMos_D1_R1 = WeMos D1 R2
  M1 = DC Motor
  S1 = H-Bridge with L298N
  M2 = DC Motor
  VCC1 = Battery block 9V
  U1 = mystery part, 3 pins [chip_label=Encoder]
  J1 = Infrared Proximity Sensor
  Part1 = 9 Degrees of Freedom - Sensor Stick  # not connected

nets:
  N1: WeMos_D1_R1.D2, S1.IN4
  N2: WeMos_D1_R1.(D5), U1.pin3
  N3: WeMos_D1_R1.(D6), S1.IN3
  N4: WeMos_D1_R1.(D7), S1.ENB
  N5: WeMos_D1_R1.D8, S1.IN2
  N6: WeMos_D1_R1.D9, S1.IN1
  N7: WeMos_D1_R1.D10, S1.ENA
  N8: WeMos_D1_R1.A0, J1.Vout
  N9: M1.pin_1, S1.M1-01
  N10: M1.pin_2, S1.M1-02
  N11: S1.12V, VCC1.+
  N12: S1.GND, VCC1.-
  N13: S1.M2-01, M2.pin_1
  N14: S1.M2-02, M2.pin_2

custom parts:
  WeMos D1 R2: The D1 R2 is a mini wifi board based on the ESP-8266EX.
  H-Bridge with L298N: h-bridge
